# Fritzing sketch loadcell (saved by Fritzing 0.9.9b)
breadboards: 1

parts:
  IC1 = PICAXE-28A [package=THT]
  パーツ1 = HX711 Weighing Sensor Module
  Power_plug1 = Power plug

nets:
  N1: IC1.In_A0, パーツ1.CK/TX
  N2: IC1.In_A1, パーツ1.DO/RX
  GND: IC1.0V, パーツ1.GND, Power_plug1.GND
  VCC: IC1.+V, パーツ1.VCC, Power_plug1.VCC
